// Logisim project circuit1a.circ as structural Verilog: 1 circuit, main circuit main
module main (
  input  A,
  input  B,
  input  C,
  output result
);

  wire ABnC, AnBC, AnBnC, nABnC, nAnBnC, not_1_out, not_2_out, not_3_out, not_4_out, not_5_out, not_6_out,
       not_7_out, not_8_out, not_9_out;

  not not_1 (not_1_out, A);
  not not_2 (not_2_out, B);
  not not_3 (not_3_out, C);
  not not_4 (not_4_out, B);
  not not_5 (not_5_out, C);
  not not_6 (not_6_out, A);
  not not_7 (not_7_out, C);
  not not_8 (not_8_out, C);
  not not_9 (not_9_out, B);
  and and_1 (nAnBnC, not_1_out, not_2_out, not_3_out);
  and and_2 (AnBnC, A, not_4_out, not_5_out);
  and and_3 (nABnC, not_6_out, B, not_7_out);
  and and_4 (ABnC, A, B, not_8_out);
  and and_5 (AnBC, A, not_9_out, C);
  or or_1 (result, nAnBnC, AnBnC, nABnC, ABnC, AnBC);
endmodule
