// Logisim project my_adder.circ as structural Verilog: 2 circuits, main circuit main
module main (
  input  [15:0] A,
  input  [15:0] B,
  input  sub,
  output [15:0] result,
  output ovf
);

  wire onebitadder_1_cout, onebitadder_2_cout, onebitadder_3_cout, onebitadder_4_cout, onebitadder_5_cout,
       onebitadder_6_cout, onebitadder_7_cout, onebitadder_8_cout, onebitadder_9_cout, onebitadder_10_cout,
       onebitadder_11_cout, onebitadder_12_cout, onebitadder_13_cout, onebitadder_14_cout,
       onebitadder_15_cout, onebitadder_16_cout, xor_1_out, xor_2_out, xor_3_out, xor_4_out, xor_5_out,
       xor_6_out, xor_7_out, xor_8_out, xor_9_out, xor_10_out, xor_11_out, xor_12_out, xor_13_out,
       xor_14_out, xor_15_out, xor_16_out;

  xor xor_1 (xor_1_out, B[0], sub);
  xor xor_2 (xor_2_out, B[4], sub);
  xor xor_3 (xor_3_out, B[8], sub);
  xor xor_4 (xor_4_out, B[12], sub);
  OneBitAdder onebitadder_1 (.Cin(sub), .a(A[0]), .b(xor_1_out), .Sum(result[0]), .Cout(onebitadder_1_cout));
  OneBitAdder onebitadder_2 (
    .Cin(onebitadder_13_cout), .a(A[4]), .b(xor_2_out), .Sum(result[4]), .Cout(onebitadder_2_cout));
  OneBitAdder onebitadder_3 (
    .Cin(onebitadder_14_cout), .a(A[8]), .b(xor_3_out), .Sum(result[8]), .Cout(onebitadder_3_cout));
  OneBitAdder onebitadder_4 (
    .Cin(onebitadder_15_cout), .a(A[12]), .b(xor_4_out), .Sum(result[12]), .Cout(onebitadder_4_cout));
  xor xor_5 (xor_5_out, B[1], sub);
  xor xor_6 (xor_6_out, B[5], sub);
  xor xor_7 (xor_7_out, B[9], sub);
  xor xor_8 (xor_8_out, B[13], sub);
  OneBitAdder onebitadder_5 (
    .Cin(onebitadder_1_cout), .a(A[1]), .b(xor_5_out), .Sum(result[1]), .Cout(onebitadder_5_cout));
  OneBitAdder onebitadder_6 (
    .Cin(onebitadder_2_cout), .a(A[5]), .b(xor_6_out), .Sum(result[5]), .Cout(onebitadder_6_cout));
  OneBitAdder onebitadder_7 (
    .Cin(onebitadder_3_cout), .a(A[9]), .b(xor_7_out), .Sum(result[9]), .Cout(onebitadder_7_cout));
  OneBitAdder onebitadder_8 (
    .Cin(onebitadder_4_cout), .a(A[13]), .b(xor_8_out), .Sum(result[13]), .Cout(onebitadder_8_cout));
  xor xor_9 (xor_9_out, B[2], sub);
  xor xor_10 (xor_10_out, B[6], sub);
  xor xor_11 (xor_11_out, B[10], sub);
  xor xor_12 (xor_12_out, B[14], sub);
  OneBitAdder onebitadder_9 (
    .Cin(onebitadder_5_cout), .a(A[2]), .b(xor_9_out), .Sum(result[2]), .Cout(onebitadder_9_cout));
  OneBitAdder onebitadder_10 (
    .Cin(onebitadder_6_cout), .a(A[6]), .b(xor_10_out), .Sum(result[6]), .Cout(onebitadder_10_cout));
  OneBitAdder onebitadder_11 (
    .Cin(onebitadder_7_cout), .a(A[10]), .b(xor_11_out), .Sum(result[10]), .Cout(onebitadder_11_cout));
  OneBitAdder onebitadder_12 (
    .Cin(onebitadder_8_cout), .a(A[14]), .b(xor_12_out), .Sum(result[14]), .Cout(onebitadder_12_cout));
  xor xor_13 (xor_13_out, B[3], sub);
  xor xor_14 (xor_14_out, B[7], sub);
  xor xor_15 (xor_15_out, B[11], sub);
  xor xor_16 (xor_16_out, B[15], sub);
  OneBitAdder onebitadder_13 (
    .Cin(onebitadder_9_cout), .a(A[3]), .b(xor_13_out), .Sum(result[3]), .Cout(onebitadder_13_cout));
  OneBitAdder onebitadder_14 (
    .Cin(onebitadder_10_cout), .a(A[7]), .b(xor_14_out), .Sum(result[7]), .Cout(onebitadder_14_cout));
  OneBitAdder onebitadder_15 (
    .Cin(onebitadder_11_cout), .a(A[11]), .b(xor_15_out), .Sum(result[11]), .Cout(onebitadder_15_cout));
  OneBitAdder onebitadder_16 (
    .Cin(onebitadder_12_cout), .a(A[15]), .b(xor_16_out), .Sum(result[15]), .Cout(onebitadder_16_cout));
  xor xor_17 (ovf, onebitadder_16_cout, onebitadder_12_cout);

  // Other names for the same wires on the sheet: S0 = result[0]; S1 = result[1]; S2 = result[2]; S3 = result[3];
  //   S4 = result[4]; S5 = result[5]; S6 = result[6]; S7 = result[7]; S8 = result[8]; S9 = result[9];
  //   S10 = result[10]; S11 = result[11]; S12 = result[12]; S13 = result[13]; S14 = result[14]; S15 = result[15]
endmodule

module OneBitAdder (
  input  Cin,
  input  a,
  input  b,
  output Sum,
  output Cout
);

  wire and_1_out, and_2_out, xor_1_out;

  and and_1 (and_1_out, b, a);
  xor xor_1 (xor_1_out, a, b);
  or or_1 (Cout, and_1_out, and_2_out);
  and and_2 (and_2_out, xor_1_out, Cin);
  xor xor_2 (Sum, Cin, xor_1_out);
endmodule
