// Logisim project press.circ as structural Verilog: 1 circuit, main circuit main
module main (
  input  go,
  input  limit,
  output motor,
  output warning
);

  wire and_1_out, and_2_out, and_3_out, and_4_out, and_5_out, and_6_out, and_7_out, and_8_out, and_9_out,
       and_10_out, and_11_out, Clock, not_1_out, not_2_out, not_3_out, not_4_out, not_5_out, not_6_out,
       not_7_out, not_8_out, not_9_out, not_10_out, not_11_out, or_1_out, or_4_out, Q0, Q1;

  and and_1 (and_1_out, go, limit);
  and and_2 (and_2_out, Q1, Q0, go);
  not not_1 (not_1_out, Q1);
  not not_2 (not_2_out, Q0);
  not not_3 (not_3_out, Q1);
  not not_4 (not_4_out, go);
  not not_5 (not_5_out, Q0);
  not not_6 (not_6_out, limit);
  not not_7 (not_7_out, Q1);
  Clock clock_1 (.out(Clock));
  and and_3 (and_3_out, not_1_out, not_2_out, go);
  and and_4 (and_4_out, not_3_out, Q0, not_4_out);
  and and_5 (and_5_out, not_5_out, go, not_6_out);
  and and_6 (and_6_out, not_7_out, go);
  or or_1 (or_1_out, and_1_out, and_2_out, and_3_out, and_4_out);
  or or_2 (motor, and_5_out, and_6_out);
  D_Flip_Flop u_Q0 (.D(or_1_out), .clk(Clock), .Q(Q0));  // open: Qn, preset, reset
  not not_8 (not_8_out, Q0);
  not not_9 (not_9_out, Q1);
  not not_10 (not_10_out, limit);
  not not_11 (not_11_out, Q0);
  and and_7 (and_7_out, Q1, not_8_out);
  and and_8 (and_8_out, not_9_out, Q0);
  and and_9 (and_9_out, Q0, go, not_10_out);
  and and_10 (and_10_out, Q1, go);
  and and_11 (and_11_out, Q1, not_11_out);
  or or_3 (warning, and_7_out, and_8_out, go);
  D_Flip_Flop u_Q1 (.D(or_4_out), .clk(Clock), .Q(Q1));  // open: Qn, preset, reset
  or or_4 (or_4_out, and_9_out, and_10_out, and_11_out);

  // Other names for the same wires on the sheet: G = go; L = limit
endmodule
