// Logisim project cpu.circ as structural Verilog: 9 circuits, main circuit main
module main (
  input  reset,
  input  [15:0] manualtest
);

  wire aand, add, addi, alu_1_equal, alu_1_less, ALUinB, and_1_out, and_2_out, ble, bne, Br, clk, DMWE,
       inpuut, J, j_t, jal, jr, keyboard_1_avail, lw, nclk, noot, not_2_out, not_3_out, or_9_out, or_10_out,
       outpuut, Rdst, RWE, slll, srll, sub, writeorreadintomem_oe_latched, writeorreadintomem_we_latched;
  wire [2:0] ALUop, multiplexer_4_out, multiplexer_5_out;
  wire [3:0] opcode;
  wire [6:0] bit_extender_3_out, keyboard_1_data;
  wire [11:0] Address;
  wire [15:0] alu_1_out1, bit_extender_1_out, bit_extender_2_out, bit_extender_4_out, branch_result,
       multiplexer_1_out, multiplexer_2_out, multiplexer_3_out, multiplexer_6_out, multiplexer_7_out,
       multiplexer_8_out, multiplexer_9_out, multiplexer_10_out, outrs, PC_out16, PCOut, ram_1_dout,
       registerfile_1_readdata2, writeorreadintomem_address_latched, writeorreadintomem_data_in_latched;

  Clock clock_1 (.out(clk));
  not not_1 (nclk, clk);
  Decoder #(.select(4)) decoder_1 (
    .out0(add), .out1(addi), .out2(sub), .out3(slll), .out4(srll), .out5(aand), .out6(noot), .out7(lw),
    .out8(DMWE), .out9(bne), .out10(ble), .out11(j_t), .out12(jr), .out13(jal), .out14(inpuut),
    .out15(outpuut), .sel(opcode));  // open: en
  SixteenBitAdder sixteenbitadder_1 (.A(PC_out16), .B(16'h1), .result(PCOut));  // open: sub, ovf
  or or_1 (RWE, srll, add, addi, sub, slll, aand, noot, lw, jal, inpuut);
  ROM #(.addrWidth(16), .dataWidth(16)) rom_1 (.addr(PC_out16), .data({opcode, Address}));
  OneRegister PC (.in16(multiplexer_8_out), .reset(reset), .clk(nclk), .RegWriteEnable(1'b1), .out16(PC_out16));
  or or_2 (Rdst, add, sub, slll, srll, aand, noot);
  or or_3 (ALUinB, addi, lw, DMWE);
  or or_4 (Br, bne, ble);
  or or_5 (J, j_t, jr, jal);
  or or_6 (ALUop[2], slll, srll);
  or or_7 (ALUop[1], aand, noot);
  Multiplexer #(.width(16), .enable("false")) multiplexer_1 (
    .in0(multiplexer_3_out), .in1(multiplexer_2_out), .out(multiplexer_1_out), .sel(inpuut));
  or or_8 (ALUop[0], sub, srll, noot);
  Keyboard #(.trigger("falling")) keyboard_1 (
    .clk(clk), .re(inpuut), .clr(reset), .avail(keyboard_1_avail), .data(keyboard_1_data));
  // Probe on multiplexer_1_out
  // Probe on Address[11:9]
  not not_2 (not_2_out, keyboard_1_avail);
  Multiplexer #(.width(16), .enable("false")) multiplexer_2 (
    .in0(bit_extender_1_out), .in1(16'h80), .out(multiplexer_2_out), .sel(not_2_out));
  Multiplexer #(.width(16), .enable("false")) multiplexer_3 (
    .in0(multiplexer_10_out), .in1(PCOut), .out(multiplexer_3_out), .sel(jal));
  // Probe on Address[8:6]
  // Probe on bit_extender_1_out
  assign bit_extender_1_out = {{9{1'b0}}, keyboard_1_data};  // Bit_Extender bit_extender_1
  // Probe on registerfile_1_readdata2
  RegisterFile registerfile_1 (
    .clk(clk), .WriteReg(multiplexer_4_out), .RegWriteEnable(RWE), .ReadReg2(Address[8:6]), .reset(reset),
    .ReadReg1(Address[11:9]), .WriteData(multiplexer_1_out), .ReadData2(registerfile_1_readdata2),
    .ReadData1(outrs));
  // Probe on multiplexer_4_out
  Multiplexer #(.width(3), .enable("false")) multiplexer_4 (
    .in0(multiplexer_5_out), .in1(3'b111), .out(multiplexer_4_out), .sel(jal));
  Multiplexer #(.width(3), .enable("false")) multiplexer_5 (
    .in0(Address[8:6]), .in1(Address[5:3]), .out(multiplexer_5_out), .sel(Rdst));
  assign bit_extender_2_out = {{10{Address[5]}}, Address[5:0]};  // Bit_Extender bit_extender_2
  // Probe on Address[5:0]
  // Probe on Address[5:3]
  // Probe on outrs
  Multiplexer #(.width(16), .enable("false")) multiplexer_6 (
    .in0(registerfile_1_readdata2), .in1(bit_extender_2_out), .out(multiplexer_6_out), .sel(ALUinB));
  // Probe on ALUop
  // Probe on multiplexer_6_out
  Bit_Extender #(.in_width(16), .out_width(7)) bit_extender_3 (.in(outrs), .out(bit_extender_3_out));
  ALU alu_1 (
    .in1(outrs), .less(alu_1_less), .Opcode(ALUop), .out1(alu_1_out1), .in2(multiplexer_6_out),
    .shift(Address[2:0]), .equal(alu_1_equal));
  TTY #(.rows(13), .cols(80)) tty_1 (.data(bit_extender_3_out), .clk(clk), .we(outpuut), .clr(reset));
  SixteenBitAdder branch (.A(PCOut), .B(bit_extender_2_out), .result(branch_result));  // open: sub, ovf
  and and_1 (and_1_out, bne, not_3_out);
  not not_3 (not_3_out, alu_1_equal);
  and and_2 (and_2_out, ble, or_9_out);
  or or_9 (or_9_out, alu_1_less, alu_1_equal);
  or or_10 (or_10_out, and_1_out, and_2_out);
  Multiplexer #(.width(16), .enable("false")) multiplexer_7 (
    .in0(PCOut), .in1(branch_result), .out(multiplexer_7_out), .sel(or_10_out));
  memory_latch writeorreadintomem (
    .address(alu_1_out1), .WE(DMWE), .clk(nclk), .data_in(registerfile_1_readdata2),
    .address_latched(writeorreadintomem_address_latched), .WE_latched(writeorreadintomem_we_latched),
    .OE_latched(writeorreadintomem_oe_latched), .data_in_latched(writeorreadintomem_data_in_latched));
  RAM #(.addrWidth(16), .dataWidth(16), .trigger("high"), .databus("bibus")) ram_1 (
    .addr(writeorreadintomem_address_latched), .we(writeorreadintomem_we_latched),
    .oe(writeorreadintomem_oe_latched), .din(writeorreadintomem_data_in_latched), .dout(ram_1_dout));
  assign bit_extender_4_out = {{4{1'b0}}, Address};  // Bit_Extender bit_extender_4
  Multiplexer #(.width(16), .enable("false")) multiplexer_8 (
    .in0(multiplexer_7_out), .in1(multiplexer_9_out), .out(multiplexer_8_out), .sel(J));
  Multiplexer #(.width(16), .enable("false")) multiplexer_9 (
    .in0(bit_extender_4_out), .in1(outrs), .out(multiplexer_9_out), .sel(jr));
  Multiplexer #(.width(16), .enable("false")) multiplexer_10 (
    .in0(alu_1_out1), .in1(ram_1_dout), .out(multiplexer_10_out), .sel(lw));

  // Other names for the same wires on the sheet: Immediate[5:0] = Address[5:0]; ROM0 = Address[0];
  //   Shamt[2:0] = Address[2:0]; ROM1 = Address[1]; ROM2 = Address[2]; Rd[2:0] = Address[5:3]; ROM3 = Address[3];
  //   ROM4 = Address[4]; ROM5 = Address[5]; ROM6 = Address[6]; Rt[2:0] = Address[8:6]; ROM7 = Address[7];
  //   ROM8 = Address[8]; ROM9 = Address[9]; Rs[2:0] = Address[11:9]; ROM10 = Address[10]; ROM11 = Address[11];
  //   ALUopBit1 = ALUop[0]; ALUopBit2 = ALUop[1]; ALUopBit3 = ALUop[2]; RWD = lw; ROM12 = opcode[0];
  //   ROM13 = opcode[1]; ROM14 = opcode[2]; ROM15 = opcode[3]; sw = DMWE

  // Notes on the sheet:
  //   contents of rom_1 (hex, n*v repeats v):
  //   104a e040 12a0 f400 e040 12a0 f400 e040 12a0 f400 a03f a504 1197 a03f 119e a03f 107f 1144 a282 1198
  //   a03f 1145
  //   rt
  //   rs
endmodule

module ALU (
  input  [15:0] in1,
  input  [2:0] Opcode,
  input  [15:0] in2,
  input  [2:0] shift,
  output [15:0] out1,
  output equal,
  output less
);

  wire not_2_out, not_3_out, not_4_out, not_5_out, not_6_out, not_7_out, not_8_out, not_9_out, not_10_out,
       not_11_out, not_12_out, not_13_out, not_14_out, not_15_out, not_16_out, not_17_out;
  wire [14:0] subtract;
  wire [15:0] aand, add, noot, oor, shiftLeft, shiftRight;

  assign noot = ~in1;  // NOT_Gate not_1, 16 bits wide
  assign oor = in1 | in2;  // OR_Gate or_1, 16 bits wide
  assign aand = in1 & in2;  // AND_Gate and_1, 16 bits wide
  not not_2 (not_2_out, subtract[8]);
  not not_3 (not_3_out, subtract[9]);
  not not_4 (not_4_out, subtract[10]);
  not not_5 (not_5_out, subtract[11]);
  not not_6 (not_6_out, subtract[12]);
  not not_7 (not_7_out, subtract[13]);
  not not_8 (not_8_out, subtract[14]);
  not not_9 (not_9_out, less);
  not not_10 (not_10_out, subtract[0]);
  not not_11 (not_11_out, subtract[1]);
  not not_12 (not_12_out, subtract[2]);
  not not_13 (not_13_out, subtract[3]);
  not not_14 (not_14_out, subtract[4]);
  not not_15 (not_15_out, subtract[5]);
  not not_16 (not_16_out, subtract[6]);
  not not_17 (not_17_out, subtract[7]);
  SixteenBitAdder sixteenbitadder_1 (.A(in1), .B(in2), .result(add));  // open: sub, ovf
  SixteenBitAdder sixteenbitadder_2 (.A(in1), .B(in2), .sub(1'b1), .result({less, subtract}));  // open: ovf
  BitShifter bitshifter_1 (.shifted(shiftLeft), .in1(in1), .shiftsize(shift));
  BitShifterR bitshifterr_1 (.in1(in1), .shiftsize(shift), .shifted(shiftRight));
  and and_2 (equal, not_10_out, not_11_out, not_12_out, not_13_out, not_14_out, not_15_out, not_16_out, not_17_out, not_2_out, not_3_out, not_4_out, not_5_out, not_6_out, not_7_out, not_8_out, not_9_out);
  Multiplexer #(.select(3), .width(16), .enable("false")) multiplexer_1 (
    .in0(add), .in1({less, subtract}), .in2(aand), .in3(noot), .in4(shiftLeft), .in5(shiftRight), .out(out1),
    .sel(Opcode));  // open: in6, in7

  // Other names for the same wires on the sheet: subtract[15] = less
endmodule

module OneBitAdder (
  input  Cin,
  input  a,
  input  b,
  output Sum,
  output Cout
);

  wire and_1_out, and_2_out, xor_1_out;

  and and_1 (and_1_out, b, a);
  xor xor_1 (xor_1_out, a, b);
  or or_1 (Cout, and_1_out, and_2_out);
  and and_2 (and_2_out, xor_1_out, Cin);
  xor xor_2 (Sum, Cin, xor_1_out);
endmodule

module SixteenBitAdder (
  input  [15:0] A,
  input  [15:0] B,
  input  sub,
  output [15:0] result,
  output ovf
);

  wire onebitadder_1_cout, onebitadder_2_cout, onebitadder_3_cout, onebitadder_4_cout, onebitadder_5_cout,
       onebitadder_6_cout, onebitadder_7_cout, onebitadder_8_cout, onebitadder_9_cout, onebitadder_10_cout,
       onebitadder_11_cout, onebitadder_12_cout, onebitadder_13_cout, onebitadder_14_cout,
       onebitadder_15_cout, onebitadder_16_cout, xor_1_out, xor_2_out, xor_3_out, xor_4_out, xor_5_out,
       xor_6_out, xor_7_out, xor_8_out, xor_9_out, xor_10_out, xor_11_out, xor_12_out, xor_13_out,
       xor_14_out, xor_15_out, xor_16_out;

  xor xor_1 (xor_1_out, B[0], sub);
  xor xor_2 (xor_2_out, B[4], sub);
  xor xor_3 (xor_3_out, B[8], sub);
  xor xor_4 (xor_4_out, B[12], sub);
  OneBitAdder onebitadder_1 (.Cin(sub), .a(A[0]), .b(xor_1_out), .Sum(result[0]), .Cout(onebitadder_1_cout));
  OneBitAdder onebitadder_2 (
    .Cin(onebitadder_13_cout), .a(A[4]), .b(xor_2_out), .Sum(result[4]), .Cout(onebitadder_2_cout));
  OneBitAdder onebitadder_3 (
    .Cin(onebitadder_14_cout), .a(A[8]), .b(xor_3_out), .Sum(result[8]), .Cout(onebitadder_3_cout));
  OneBitAdder onebitadder_4 (
    .Cin(onebitadder_15_cout), .a(A[12]), .b(xor_4_out), .Sum(result[12]), .Cout(onebitadder_4_cout));
  xor xor_5 (xor_5_out, B[1], sub);
  xor xor_6 (xor_6_out, B[5], sub);
  xor xor_7 (xor_7_out, B[9], sub);
  xor xor_8 (xor_8_out, B[13], sub);
  OneBitAdder onebitadder_5 (
    .Cin(onebitadder_1_cout), .a(A[1]), .b(xor_5_out), .Sum(result[1]), .Cout(onebitadder_5_cout));
  OneBitAdder onebitadder_6 (
    .Cin(onebitadder_2_cout), .a(A[5]), .b(xor_6_out), .Sum(result[5]), .Cout(onebitadder_6_cout));
  OneBitAdder onebitadder_7 (
    .Cin(onebitadder_3_cout), .a(A[9]), .b(xor_7_out), .Sum(result[9]), .Cout(onebitadder_7_cout));
  OneBitAdder onebitadder_8 (
    .Cin(onebitadder_4_cout), .a(A[13]), .b(xor_8_out), .Sum(result[13]), .Cout(onebitadder_8_cout));
  xor xor_9 (xor_9_out, B[2], sub);
  xor xor_10 (xor_10_out, B[6], sub);
  xor xor_11 (xor_11_out, B[10], sub);
  xor xor_12 (xor_12_out, B[14], sub);
  OneBitAdder onebitadder_9 (
    .Cin(onebitadder_5_cout), .a(A[2]), .b(xor_9_out), .Sum(result[2]), .Cout(onebitadder_9_cout));
  OneBitAdder onebitadder_10 (
    .Cin(onebitadder_6_cout), .a(A[6]), .b(xor_10_out), .Sum(result[6]), .Cout(onebitadder_10_cout));
  OneBitAdder onebitadder_11 (
    .Cin(onebitadder_7_cout), .a(A[10]), .b(xor_11_out), .Sum(result[10]), .Cout(onebitadder_11_cout));
  OneBitAdder onebitadder_12 (
    .Cin(onebitadder_8_cout), .a(A[14]), .b(xor_12_out), .Sum(result[14]), .Cout(onebitadder_12_cout));
  xor xor_13 (xor_13_out, B[3], sub);
  xor xor_14 (xor_14_out, B[7], sub);
  xor xor_15 (xor_15_out, B[11], sub);
  xor xor_16 (xor_16_out, B[15], sub);
  OneBitAdder onebitadder_13 (
    .Cin(onebitadder_9_cout), .a(A[3]), .b(xor_13_out), .Sum(result[3]), .Cout(onebitadder_13_cout));
  OneBitAdder onebitadder_14 (
    .Cin(onebitadder_10_cout), .a(A[7]), .b(xor_14_out), .Sum(result[7]), .Cout(onebitadder_14_cout));
  OneBitAdder onebitadder_15 (
    .Cin(onebitadder_11_cout), .a(A[11]), .b(xor_15_out), .Sum(result[11]), .Cout(onebitadder_15_cout));
  OneBitAdder onebitadder_16 (
    .Cin(onebitadder_12_cout), .a(A[15]), .b(xor_16_out), .Sum(result[15]), .Cout(onebitadder_16_cout));
  xor xor_17 (ovf, onebitadder_16_cout, onebitadder_12_cout);

  // Other names for the same wires on the sheet: S0 = result[0]; S1 = result[1]; S2 = result[2]; S3 = result[3];
  //   S4 = result[4]; S5 = result[5]; S6 = result[6]; S7 = result[7]; S8 = result[8]; S9 = result[9];
  //   S10 = result[10]; S11 = result[11]; S12 = result[12]; S13 = result[13]; S14 = result[14]; S15 = result[15]
endmodule

module memory_latch (
  input  [15:0] address,
  input  WE,
  input  clk,
  input  [15:0] data_in,
  output [15:0] address_latched,
  output WE_latched,
  output OE_latched,
  output [15:0] data_in_latched
);

  wire DMwe_latch_q;
  wire [15:0] addr_latch_q;

  Register #(.width(16), .trigger("falling")) addr_latch (
    .D(address), .en(WE), .clk(clk), .Q(addr_latch_q));  // open: clr
  D_Flip_Flop #(.trigger("falling")) DMwe_latch (.D(WE), .clk(clk), .Q(DMwe_latch_q));  // open: Qn, preset, reset
  Register #(.width(16), .trigger("falling")) data_to_be_written (
    .D(data_in), .en(WE), .clk(clk), .Q(data_in_latched));  // open: clr
  Multiplexer #(.width(16), .enable("false")) multiplexer_1 (
    .in0(address), .in1(addr_latch_q), .out(address_latched), .sel(DMwe_latch_q));
  and and_1 (WE_latched, clk, DMwe_latch_q);
  not not_1 (OE_latched, WE_latched);
endmodule

module RegisterFile (
  input  [15:0] WriteData,
  input  clk,
  input  RegWriteEnable,
  input  reset,
  input  [2:0] ReadReg1,
  input  [2:0] ReadReg2,
  input  [2:0] WriteReg,
  output [15:0] ReadData2,
  output [15:0] ReadData1
);

  wire reg1_0, reg1_1, reg1_2, reg1_3, reg1_4, reg1_5, reg1_6, reg1_7, reg2_0, reg2_1, reg2_2, reg2_3,
       reg2_4, reg2_5, reg2_6, reg2_7, write0, write1, write2, write3, write4, write5, write6, write7;
  wire [15:0] oneregister_1_out16, oneregister_2_out16, oneregister_3_out16, oneregister_4_out16,
       oneregister_5_out16, oneregister_6_out16, oneregister_7_out16, oneregister_8_out16;

  OneRegister oneregister_1 (
    .in16(WriteData), .reset(reset), .clk(clk), .RegWriteEnable(1'b0), .out16(oneregister_1_out16));
  assign ReadData1 = reg1_0 ? oneregister_1_out16 : 16'bz;  // Controlled_Buffer controlled_buffer_1
  assign ReadData2 = reg2_0 ? oneregister_1_out16 : 16'bz;  // Controlled_Buffer controlled_buffer_2
  OneRegister oneregister_2 (
    .in16(WriteData), .reset(reset), .clk(clk), .RegWriteEnable(write1), .out16(oneregister_2_out16));
  assign ReadData1 = reg1_1 ? oneregister_2_out16 : 16'bz;  // Controlled_Buffer controlled_buffer_3
  assign ReadData2 = reg2_1 ? oneregister_2_out16 : 16'bz;  // Controlled_Buffer controlled_buffer_4
  OneRegister oneregister_3 (
    .in16(WriteData), .reset(reset), .clk(clk), .RegWriteEnable(write2), .out16(oneregister_3_out16));
  assign ReadData1 = reg1_2 ? oneregister_3_out16 : 16'bz;  // Controlled_Buffer controlled_buffer_5
  assign ReadData2 = reg2_2 ? oneregister_3_out16 : 16'bz;  // Controlled_Buffer controlled_buffer_6
  OneRegister oneregister_4 (
    .in16(WriteData), .reset(reset), .clk(clk), .RegWriteEnable(write3), .out16(oneregister_4_out16));
  assign ReadData1 = reg1_3 ? oneregister_4_out16 : 16'bz;  // Controlled_Buffer controlled_buffer_7
  assign ReadData2 = reg2_3 ? oneregister_4_out16 : 16'bz;  // Controlled_Buffer controlled_buffer_8
  OneRegister oneregister_5 (
    .in16(WriteData), .reset(reset), .clk(clk), .RegWriteEnable(write4), .out16(oneregister_5_out16));
  assign ReadData1 = reg1_4 ? oneregister_5_out16 : 16'bz;  // Controlled_Buffer controlled_buffer_9
  assign ReadData2 = reg2_4 ? oneregister_5_out16 : 16'bz;  // Controlled_Buffer controlled_buffer_10
  assign ReadData1 = reg1_5 ? oneregister_6_out16 : 16'bz;  // Controlled_Buffer controlled_buffer_11
  OneRegister oneregister_6 (
    .in16(WriteData), .reset(reset), .clk(clk), .RegWriteEnable(write5), .out16(oneregister_6_out16));
  assign ReadData2 = reg2_5 ? oneregister_6_out16 : 16'bz;  // Controlled_Buffer controlled_buffer_12
  OneRegister oneregister_7 (
    .in16(WriteData), .reset(reset), .clk(clk), .RegWriteEnable(write6), .out16(oneregister_7_out16));
  assign ReadData1 = reg1_6 ? oneregister_7_out16 : 16'bz;  // Controlled_Buffer controlled_buffer_13
  assign ReadData2 = reg2_6 ? oneregister_7_out16 : 16'bz;  // Controlled_Buffer controlled_buffer_14
  assign ReadData1 = reg1_7 ? oneregister_8_out16 : 16'bz;  // Controlled_Buffer controlled_buffer_15
  OneRegister oneregister_8 (
    .in16(WriteData), .reset(reset), .clk(clk), .RegWriteEnable(write7), .out16(oneregister_8_out16));
  assign ReadData2 = reg2_7 ? oneregister_8_out16 : 16'bz;  // Controlled_Buffer controlled_buffer_16
  Decoder #(.select(3)) decoder_1 (
    .out0(reg1_0), .out1(reg1_1), .out2(reg1_2), .out3(reg1_3), .out4(reg1_4), .out5(reg1_5), .out6(reg1_6),
    .out7(reg1_7), .sel(ReadReg1));  // open: en
  // Probe on oneregister_1_out16
  // Probe on oneregister_2_out16
  // Probe on oneregister_3_out16
  // Probe on oneregister_4_out16
  // Probe on oneregister_5_out16
  // Probe on oneregister_6_out16
  // Probe on oneregister_7_out16
  // Probe on oneregister_8_out16
  Decoder #(.select(3)) decoder_2 (
    .out0(reg2_0), .out1(reg2_1), .out2(reg2_2), .out3(reg2_3), .out4(reg2_4), .out5(reg2_5), .out6(reg2_6),
    .out7(reg2_7), .sel(ReadReg2));  // open: en
  Decoder #(.select(3)) decoder_3 (
    .out0(write0), .out1(write1), .out2(write2), .out3(write3), .out4(write4), .out5(write5), .out6(write6),
    .out7(write7), .sel(WriteReg), .en(RegWriteEnable));

  // Other names for the same wires on the sheet: data_in[15:0] = WriteData

  // Notes on the sheet:
  //   rt out
  //   rs out
endmodule

module OneRegister (
  input  [15:0] in16,
  input  reset,
  input  clk,
  input  RegWriteEnable,
  output [15:0] out16
);

  wire ClockedWriteEnable;

  D_Flip_Flop d_ff_1 (.D(in16[0]), .clk(ClockedWriteEnable), .Q(out16[0]), .reset(reset));  // open: Qn, preset
  D_Flip_Flop d_ff_2 (.D(in16[1]), .clk(ClockedWriteEnable), .Q(out16[1]), .reset(reset));  // open: Qn, preset
  D_Flip_Flop d_ff_3 (.D(in16[2]), .clk(ClockedWriteEnable), .Q(out16[2]), .reset(reset));  // open: Qn, preset
  D_Flip_Flop d_ff_4 (.D(in16[3]), .clk(ClockedWriteEnable), .Q(out16[3]), .reset(reset));  // open: Qn, preset
  D_Flip_Flop d_ff_5 (.D(in16[4]), .clk(ClockedWriteEnable), .Q(out16[4]), .reset(reset));  // open: Qn, preset
  D_Flip_Flop d_ff_6 (.D(in16[5]), .clk(ClockedWriteEnable), .Q(out16[5]), .reset(reset));  // open: Qn, preset
  D_Flip_Flop d_ff_7 (.D(in16[6]), .clk(ClockedWriteEnable), .Q(out16[6]), .reset(reset));  // open: Qn, preset
  D_Flip_Flop d_ff_8 (.D(in16[7]), .clk(ClockedWriteEnable), .Q(out16[7]), .reset(reset));  // open: Qn, preset
  and and_1 (ClockedWriteEnable, clk, RegWriteEnable);
  D_Flip_Flop d_ff_9 (.D(in16[8]), .clk(ClockedWriteEnable), .Q(out16[8]), .reset(reset));  // open: Qn, preset
  D_Flip_Flop d_ff_10 (.D(in16[9]), .clk(ClockedWriteEnable), .Q(out16[9]), .reset(reset));  // open: Qn, preset
  D_Flip_Flop d_ff_11 (.D(in16[10]), .clk(ClockedWriteEnable), .Q(out16[10]), .reset(reset));  // open: Qn, preset
  D_Flip_Flop d_ff_12 (.D(in16[11]), .clk(ClockedWriteEnable), .Q(out16[11]), .reset(reset));  // open: Qn, preset
  D_Flip_Flop d_ff_13 (.D(in16[12]), .clk(ClockedWriteEnable), .Q(out16[12]), .reset(reset));  // open: Qn, preset
  D_Flip_Flop d_ff_14 (.D(in16[13]), .clk(ClockedWriteEnable), .Q(out16[13]), .reset(reset));  // open: Qn, preset
  D_Flip_Flop d_ff_15 (.D(in16[14]), .clk(ClockedWriteEnable), .Q(out16[14]), .reset(reset));  // open: Qn, preset
  D_Flip_Flop d_ff_16 (.D(in16[15]), .clk(ClockedWriteEnable), .Q(out16[15]), .reset(reset));  // open: Qn, preset

  // Other names for the same wires on the sheet: W0 = in16[0]; W1 = in16[1]; W2 = in16[2]; W3 = in16[3]; W4 = in16[4];
  //   W5 = in16[5]; W6 = in16[6]; W7 = in16[7]; W8 = in16[8]; W9 = in16[9]; W10 = in16[10]; W11 = in16[11];
  //   W12 = in16[12]; W13 = in16[13]; W14 = in16[14]; W15 = in16[15]; R0 = out16[0]; R1 = out16[1]; R2 = out16[2];
  //   R3 = out16[3]; R4 = out16[4]; R5 = out16[5]; R6 = out16[6]; R7 = out16[7]; R8 = out16[8]; R9 = out16[9];
  //   R10 = out16[10]; R11 = out16[11]; R12 = out16[12]; R13 = out16[13]; R14 = out16[14]; R15 = out16[15]
endmodule

module BitShifter (
  input  [15:0] in1,
  input  [2:0] shiftsize,
  output [15:0] shifted
);

  wire multiplexer_1_out, multiplexer_2_out, multiplexer_3_out, multiplexer_4_out, multiplexer_5_out,
       multiplexer_6_out, multiplexer_7_out, multiplexer_8_out, multiplexer_9_out, multiplexer_10_out,
       multiplexer_11_out, multiplexer_12_out, multiplexer_13_out, multiplexer_14_out, multiplexer_15_out,
       multiplexer_16_out, multiplexer_17_out, multiplexer_18_out, multiplexer_19_out, multiplexer_20_out,
       multiplexer_21_out, multiplexer_22_out, multiplexer_23_out, multiplexer_24_out, multiplexer_25_out,
       multiplexer_26_out, multiplexer_27_out, multiplexer_28_out, multiplexer_29_out, multiplexer_30_out,
       multiplexer_31_out, multiplexer_32_out;

  Multiplexer #(.enable("false")) multiplexer_1 (
    .in0(in1[15]), .in1(in1[11]), .out(multiplexer_1_out), .sel(shiftsize[2]));
  Multiplexer #(.enable("false")) multiplexer_2 (
    .in0(in1[14]), .in1(in1[10]), .out(multiplexer_2_out), .sel(shiftsize[2]));
  Multiplexer #(.enable("false")) multiplexer_3 (
    .in0(in1[13]), .in1(in1[9]), .out(multiplexer_3_out), .sel(shiftsize[2]));
  Multiplexer #(.enable("false")) multiplexer_4 (
    .in0(in1[12]), .in1(in1[8]), .out(multiplexer_4_out), .sel(shiftsize[2]));
  Multiplexer #(.enable("false")) multiplexer_5 (
    .in0(in1[11]), .in1(in1[7]), .out(multiplexer_5_out), .sel(shiftsize[2]));
  Multiplexer #(.enable("false")) multiplexer_6 (
    .in0(in1[10]), .in1(in1[6]), .out(multiplexer_6_out), .sel(shiftsize[2]));
  Multiplexer #(.enable("false")) multiplexer_7 (
    .in0(in1[9]), .in1(in1[5]), .out(multiplexer_7_out), .sel(shiftsize[2]));
  Multiplexer #(.enable("false")) multiplexer_8 (
    .in0(in1[8]), .in1(in1[4]), .out(multiplexer_8_out), .sel(shiftsize[2]));
  Multiplexer #(.enable("false")) multiplexer_9 (
    .in0(in1[7]), .in1(in1[3]), .out(multiplexer_9_out), .sel(shiftsize[2]));
  Multiplexer #(.enable("false")) multiplexer_10 (
    .in0(in1[6]), .in1(in1[2]), .out(multiplexer_10_out), .sel(shiftsize[2]));
  Multiplexer #(.enable("false")) multiplexer_11 (
    .in0(in1[5]), .in1(in1[1]), .out(multiplexer_11_out), .sel(shiftsize[2]));
  Multiplexer #(.enable("false")) multiplexer_12 (
    .in0(in1[4]), .in1(in1[0]), .out(multiplexer_12_out), .sel(shiftsize[2]));
  Multiplexer #(.enable("false")) multiplexer_13 (
    .in0(in1[3]), .in1(1'b0), .out(multiplexer_13_out), .sel(shiftsize[2]));
  Multiplexer #(.enable("false")) multiplexer_14 (
    .in0(in1[2]), .in1(1'b0), .out(multiplexer_14_out), .sel(shiftsize[2]));
  Multiplexer #(.enable("false")) multiplexer_15 (
    .in0(in1[1]), .in1(1'b0), .out(multiplexer_15_out), .sel(shiftsize[2]));
  Multiplexer #(.enable("false")) multiplexer_16 (
    .in0(in1[0]), .in1(1'b0), .out(multiplexer_16_out), .sel(shiftsize[2]));
  Multiplexer #(.enable("false")) multiplexer_17 (
    .in0(multiplexer_1_out), .in1(multiplexer_3_out), .out(multiplexer_17_out), .sel(shiftsize[1]));
  Multiplexer #(.enable("false")) multiplexer_18 (
    .in0(multiplexer_2_out), .in1(multiplexer_4_out), .out(multiplexer_18_out), .sel(shiftsize[1]));
  Multiplexer #(.enable("false")) multiplexer_19 (
    .in0(multiplexer_3_out), .in1(multiplexer_5_out), .out(multiplexer_19_out), .sel(shiftsize[1]));
  Multiplexer #(.enable("false")) multiplexer_20 (
    .in0(multiplexer_4_out), .in1(multiplexer_6_out), .out(multiplexer_20_out), .sel(shiftsize[1]));
  Multiplexer #(.enable("false")) multiplexer_21 (
    .in0(multiplexer_5_out), .in1(multiplexer_7_out), .out(multiplexer_21_out), .sel(shiftsize[1]));
  Multiplexer #(.enable("false")) multiplexer_22 (
    .in0(multiplexer_6_out), .in1(multiplexer_8_out), .out(multiplexer_22_out), .sel(shiftsize[1]));
  Multiplexer #(.enable("false")) multiplexer_23 (
    .in0(multiplexer_7_out), .in1(multiplexer_9_out), .out(multiplexer_23_out), .sel(shiftsize[1]));
  Multiplexer #(.enable("false")) multiplexer_24 (
    .in0(multiplexer_8_out), .in1(multiplexer_10_out), .out(multiplexer_24_out), .sel(shiftsize[1]));
  Multiplexer #(.enable("false")) multiplexer_25 (
    .in0(multiplexer_9_out), .in1(multiplexer_11_out), .out(multiplexer_25_out), .sel(shiftsize[1]));
  Multiplexer #(.enable("false")) multiplexer_26 (
    .in0(multiplexer_10_out), .in1(multiplexer_12_out), .out(multiplexer_26_out), .sel(shiftsize[1]));
  Multiplexer #(.enable("false")) multiplexer_27 (
    .in0(multiplexer_11_out), .in1(multiplexer_13_out), .out(multiplexer_27_out), .sel(shiftsize[1]));
  Multiplexer #(.enable("false")) multiplexer_28 (
    .in0(multiplexer_12_out), .in1(multiplexer_14_out), .out(multiplexer_28_out), .sel(shiftsize[1]));
  Multiplexer #(.enable("false")) multiplexer_29 (
    .in0(multiplexer_13_out), .in1(multiplexer_15_out), .out(multiplexer_29_out), .sel(shiftsize[1]));
  Multiplexer #(.enable("false")) multiplexer_30 (
    .in0(multiplexer_14_out), .in1(multiplexer_16_out), .out(multiplexer_30_out), .sel(shiftsize[1]));
  Multiplexer #(.enable("false")) multiplexer_31 (
    .in0(multiplexer_15_out), .in1(1'b0), .out(multiplexer_31_out), .sel(shiftsize[1]));
  Multiplexer #(.enable("false")) multiplexer_32 (
    .in0(multiplexer_16_out), .in1(1'b0), .out(multiplexer_32_out), .sel(shiftsize[1]));
  Multiplexer #(.enable("false")) multiplexer_33 (
    .in0(multiplexer_17_out), .in1(multiplexer_18_out), .out(shifted[15]), .sel(shiftsize[0]));
  Multiplexer #(.enable("false")) multiplexer_34 (
    .in0(multiplexer_18_out), .in1(multiplexer_19_out), .out(shifted[14]), .sel(shiftsize[0]));
  Multiplexer #(.enable("false")) multiplexer_35 (
    .in0(multiplexer_19_out), .in1(multiplexer_20_out), .out(shifted[13]), .sel(shiftsize[0]));
  Multiplexer #(.enable("false")) multiplexer_36 (
    .in0(multiplexer_20_out), .in1(multiplexer_21_out), .out(shifted[12]), .sel(shiftsize[0]));
  Multiplexer #(.enable("false")) multiplexer_37 (
    .in0(multiplexer_21_out), .in1(multiplexer_22_out), .out(shifted[11]), .sel(shiftsize[0]));
  Multiplexer #(.enable("false")) multiplexer_38 (
    .in0(multiplexer_22_out), .in1(multiplexer_23_out), .out(shifted[10]), .sel(shiftsize[0]));
  Multiplexer #(.enable("false")) multiplexer_39 (
    .in0(multiplexer_23_out), .in1(multiplexer_24_out), .out(shifted[9]), .sel(shiftsize[0]));
  Multiplexer #(.enable("false")) multiplexer_40 (
    .in0(multiplexer_24_out), .in1(multiplexer_25_out), .out(shifted[8]), .sel(shiftsize[0]));
  Multiplexer #(.enable("false")) multiplexer_41 (
    .in0(multiplexer_25_out), .in1(multiplexer_26_out), .out(shifted[7]), .sel(shiftsize[0]));
  Multiplexer #(.enable("false")) multiplexer_42 (
    .in0(multiplexer_26_out), .in1(multiplexer_27_out), .out(shifted[6]), .sel(shiftsize[0]));
  Multiplexer #(.enable("false")) multiplexer_43 (
    .in0(multiplexer_27_out), .in1(multiplexer_28_out), .out(shifted[5]), .sel(shiftsize[0]));
  Multiplexer #(.enable("false")) multiplexer_44 (
    .in0(multiplexer_28_out), .in1(multiplexer_29_out), .out(shifted[4]), .sel(shiftsize[0]));
  Multiplexer #(.enable("false")) multiplexer_45 (
    .in0(multiplexer_29_out), .in1(multiplexer_30_out), .out(shifted[3]), .sel(shiftsize[0]));
  Multiplexer #(.enable("false")) multiplexer_46 (
    .in0(multiplexer_30_out), .in1(multiplexer_31_out), .out(shifted[2]), .sel(shiftsize[0]));
  Multiplexer #(.enable("false")) multiplexer_47 (
    .in0(multiplexer_31_out), .in1(multiplexer_32_out), .out(shifted[1]), .sel(shiftsize[0]));
  Multiplexer #(.enable("false")) multiplexer_48 (
    .in0(multiplexer_32_out), .in1(1'b0), .out(shifted[0]), .sel(shiftsize[0]));

  // Other names for the same wires on the sheet: W0 = in1[0]; W1 = in1[1]; W2 = in1[2]; W3 = in1[3]; W4 = in1[4];
  //   W5 = in1[5]; W6 = in1[6]; W7 = in1[7]; W8 = in1[8]; W9 = in1[9]; W10 = in1[10]; W11 = in1[11]; W12 = in1[12];
  //   W13 = in1[13]; W14 = in1[14]; W15 = in1[15]; R0 = shifted[0]; R1 = shifted[1]; R2 = shifted[2]; R3 = shifted[3];
  //   R4 = shifted[4]; R5 = shifted[5]; R6 = shifted[6]; R7 = shifted[7]; R8 = shifted[8]; R9 = shifted[9];
  //   R10 = shifted[10]; R11 = shifted[11]; R12 = shifted[12]; R13 = shifted[13]; R14 = shifted[14];
  //   R15 = shifted[15]; S1 = shiftsize[0]; S2 = shiftsize[1]; S3 = shiftsize[2]
endmodule

module BitShifterR (
  input  [15:0] in1,
  input  [2:0] shiftsize,
  output [15:0] shifted
);

  wire multiplexer_1_out, multiplexer_2_out, multiplexer_3_out, multiplexer_4_out, multiplexer_5_out,
       multiplexer_6_out, multiplexer_7_out, multiplexer_8_out, multiplexer_9_out, multiplexer_10_out,
       multiplexer_11_out, multiplexer_12_out, multiplexer_13_out, multiplexer_14_out, multiplexer_15_out,
       multiplexer_16_out, multiplexer_17_out, multiplexer_18_out, multiplexer_19_out, multiplexer_20_out,
       multiplexer_21_out, multiplexer_22_out, multiplexer_23_out, multiplexer_24_out, multiplexer_25_out,
       multiplexer_26_out, multiplexer_27_out, multiplexer_28_out, multiplexer_29_out, multiplexer_30_out,
       multiplexer_31_out, multiplexer_32_out;

  Multiplexer #(.enable("false")) multiplexer_1 (
    .in0(in1[0]), .in1(in1[4]), .out(multiplexer_1_out), .sel(shiftsize[2]));
  Multiplexer #(.enable("false")) multiplexer_2 (
    .in0(in1[1]), .in1(in1[5]), .out(multiplexer_2_out), .sel(shiftsize[2]));
  Multiplexer #(.enable("false")) multiplexer_3 (
    .in0(in1[2]), .in1(in1[6]), .out(multiplexer_3_out), .sel(shiftsize[2]));
  Multiplexer #(.enable("false")) multiplexer_4 (
    .in0(in1[3]), .in1(in1[7]), .out(multiplexer_4_out), .sel(shiftsize[2]));
  Multiplexer #(.enable("false")) multiplexer_5 (
    .in0(in1[4]), .in1(in1[8]), .out(multiplexer_5_out), .sel(shiftsize[2]));
  Multiplexer #(.enable("false")) multiplexer_6 (
    .in0(in1[5]), .in1(in1[9]), .out(multiplexer_6_out), .sel(shiftsize[2]));
  Multiplexer #(.enable("false")) multiplexer_7 (
    .in0(in1[6]), .in1(in1[10]), .out(multiplexer_7_out), .sel(shiftsize[2]));
  Multiplexer #(.enable("false")) multiplexer_8 (
    .in0(in1[7]), .in1(in1[11]), .out(multiplexer_8_out), .sel(shiftsize[2]));
  Multiplexer #(.enable("false")) multiplexer_9 (
    .in0(in1[8]), .in1(in1[12]), .out(multiplexer_9_out), .sel(shiftsize[2]));
  Multiplexer #(.enable("false")) multiplexer_10 (
    .in0(in1[9]), .in1(in1[13]), .out(multiplexer_10_out), .sel(shiftsize[2]));
  Multiplexer #(.enable("false")) multiplexer_11 (
    .in0(in1[10]), .in1(in1[14]), .out(multiplexer_11_out), .sel(shiftsize[2]));
  Multiplexer #(.enable("false")) multiplexer_12 (
    .in0(in1[11]), .in1(in1[15]), .out(multiplexer_12_out), .sel(shiftsize[2]));
  Multiplexer #(.enable("false")) multiplexer_13 (
    .in0(in1[12]), .in1(1'b0), .out(multiplexer_13_out), .sel(shiftsize[2]));
  Multiplexer #(.enable("false")) multiplexer_14 (
    .in0(in1[13]), .in1(1'b0), .out(multiplexer_14_out), .sel(shiftsize[2]));
  Multiplexer #(.enable("false")) multiplexer_15 (
    .in0(in1[14]), .in1(1'b0), .out(multiplexer_15_out), .sel(shiftsize[2]));
  Multiplexer #(.enable("false")) multiplexer_16 (
    .in0(in1[15]), .in1(1'b0), .out(multiplexer_16_out), .sel(shiftsize[2]));
  Multiplexer #(.enable("false")) multiplexer_17 (
    .in0(multiplexer_1_out), .in1(multiplexer_3_out), .out(multiplexer_17_out), .sel(shiftsize[1]));
  Multiplexer #(.enable("false")) multiplexer_18 (
    .in0(multiplexer_2_out), .in1(multiplexer_4_out), .out(multiplexer_18_out), .sel(shiftsize[1]));
  Multiplexer #(.enable("false")) multiplexer_19 (
    .in0(multiplexer_3_out), .in1(multiplexer_5_out), .out(multiplexer_19_out), .sel(shiftsize[1]));
  Multiplexer #(.enable("false")) multiplexer_20 (
    .in0(multiplexer_4_out), .in1(multiplexer_6_out), .out(multiplexer_20_out), .sel(shiftsize[1]));
  Multiplexer #(.enable("false")) multiplexer_21 (
    .in0(multiplexer_5_out), .in1(multiplexer_7_out), .out(multiplexer_21_out), .sel(shiftsize[1]));
  Multiplexer #(.enable("false")) multiplexer_22 (
    .in0(multiplexer_6_out), .in1(multiplexer_8_out), .out(multiplexer_22_out), .sel(shiftsize[1]));
  Multiplexer #(.enable("false")) multiplexer_23 (
    .in0(multiplexer_7_out), .in1(multiplexer_9_out), .out(multiplexer_23_out), .sel(shiftsize[1]));
  Multiplexer #(.enable("false")) multiplexer_24 (
    .in0(multiplexer_8_out), .in1(multiplexer_10_out), .out(multiplexer_24_out), .sel(shiftsize[1]));
  Multiplexer #(.enable("false")) multiplexer_25 (
    .in0(multiplexer_9_out), .in1(multiplexer_11_out), .out(multiplexer_25_out), .sel(shiftsize[1]));
  Multiplexer #(.enable("false")) multiplexer_26 (
    .in0(multiplexer_10_out), .in1(multiplexer_12_out), .out(multiplexer_26_out), .sel(shiftsize[1]));
  Multiplexer #(.enable("false")) multiplexer_27 (
    .in0(multiplexer_11_out), .in1(multiplexer_13_out), .out(multiplexer_27_out), .sel(shiftsize[1]));
  Multiplexer #(.enable("false")) multiplexer_28 (
    .in0(multiplexer_12_out), .in1(multiplexer_14_out), .out(multiplexer_28_out), .sel(shiftsize[1]));
  Multiplexer #(.enable("false")) multiplexer_29 (
    .in0(multiplexer_13_out), .in1(multiplexer_15_out), .out(multiplexer_29_out), .sel(shiftsize[1]));
  Multiplexer #(.enable("false")) multiplexer_30 (
    .in0(multiplexer_14_out), .in1(multiplexer_16_out), .out(multiplexer_30_out), .sel(shiftsize[1]));
  Multiplexer #(.enable("false")) multiplexer_31 (
    .in0(multiplexer_15_out), .in1(1'b0), .out(multiplexer_31_out), .sel(shiftsize[1]));
  Multiplexer #(.enable("false")) multiplexer_32 (
    .in0(multiplexer_16_out), .in1(1'b0), .out(multiplexer_32_out), .sel(shiftsize[1]));
  Multiplexer #(.enable("false")) multiplexer_33 (
    .in0(multiplexer_17_out), .in1(multiplexer_18_out), .out(shifted[0]), .sel(shiftsize[0]));
  Multiplexer #(.enable("false")) multiplexer_34 (
    .in0(multiplexer_18_out), .in1(multiplexer_19_out), .out(shifted[1]), .sel(shiftsize[0]));
  Multiplexer #(.enable("false")) multiplexer_35 (
    .in0(multiplexer_19_out), .in1(multiplexer_20_out), .out(shifted[2]), .sel(shiftsize[0]));
  Multiplexer #(.enable("false")) multiplexer_36 (
    .in0(multiplexer_20_out), .in1(multiplexer_21_out), .out(shifted[3]), .sel(shiftsize[0]));
  Multiplexer #(.enable("false")) multiplexer_37 (
    .in0(multiplexer_21_out), .in1(multiplexer_22_out), .out(shifted[4]), .sel(shiftsize[0]));
  Multiplexer #(.enable("false")) multiplexer_38 (
    .in0(multiplexer_22_out), .in1(multiplexer_23_out), .out(shifted[5]), .sel(shiftsize[0]));
  Multiplexer #(.enable("false")) multiplexer_39 (
    .in0(multiplexer_23_out), .in1(multiplexer_24_out), .out(shifted[6]), .sel(shiftsize[0]));
  Multiplexer #(.enable("false")) multiplexer_40 (
    .in0(multiplexer_24_out), .in1(multiplexer_25_out), .out(shifted[7]), .sel(shiftsize[0]));
  Multiplexer #(.enable("false")) multiplexer_41 (
    .in0(multiplexer_25_out), .in1(multiplexer_26_out), .out(shifted[8]), .sel(shiftsize[0]));
  Multiplexer #(.enable("false")) multiplexer_42 (
    .in0(multiplexer_26_out), .in1(multiplexer_27_out), .out(shifted[9]), .sel(shiftsize[0]));
  Multiplexer #(.enable("false")) multiplexer_43 (
    .in0(multiplexer_27_out), .in1(multiplexer_28_out), .out(shifted[10]), .sel(shiftsize[0]));
  Multiplexer #(.enable("false")) multiplexer_44 (
    .in0(multiplexer_28_out), .in1(multiplexer_29_out), .out(shifted[11]), .sel(shiftsize[0]));
  Multiplexer #(.enable("false")) multiplexer_45 (
    .in0(multiplexer_29_out), .in1(multiplexer_30_out), .out(shifted[12]), .sel(shiftsize[0]));
  Multiplexer #(.enable("false")) multiplexer_46 (
    .in0(multiplexer_30_out), .in1(multiplexer_31_out), .out(shifted[13]), .sel(shiftsize[0]));
  Multiplexer #(.enable("false")) multiplexer_47 (
    .in0(multiplexer_31_out), .in1(multiplexer_32_out), .out(shifted[14]), .sel(shiftsize[0]));
  Multiplexer #(.enable("false")) multiplexer_48 (
    .in0(multiplexer_32_out), .in1(1'b0), .out(shifted[15]), .sel(shiftsize[0]));

  // Other names for the same wires on the sheet: W0 = in1[0]; W1 = in1[1]; W2 = in1[2]; W3 = in1[3]; W4 = in1[4];
  //   W5 = in1[5]; W6 = in1[6]; W7 = in1[7]; W8 = in1[8]; W9 = in1[9]; W10 = in1[10]; W11 = in1[11]; W12 = in1[12];
  //   W13 = in1[13]; W14 = in1[14]; W15 = in1[15]; R0 = shifted[0]; R1 = shifted[1]; R2 = shifted[2]; R3 = shifted[3];
  //   R4 = shifted[4]; R5 = shifted[5]; R6 = shifted[6]; R7 = shifted[7]; R8 = shifted[8]; R9 = shifted[9];
  //   R10 = shifted[10]; R11 = shifted[11]; R12 = shifted[12]; R13 = shifted[13]; R14 = shifted[14];
  //   R15 = shifted[15]; S1 = shiftsize[0]; S2 = shiftsize[1]; S3 = shiftsize[2]
endmodule
