// Logisim project adder.circ as structural Verilog: 1 circuit, main circuit main
module main (
  input  in_1,
  input  in_2,
  input  in_3,
  output out_4
);

  wire and_1_out, and_2_out, xor_1_out;

  and and_1 (and_1_out, in_3, in_2);
  xor xor_1 (xor_1_out, in_2, in_3);
  // OR_Gate or_1 has open pins: in0=and_1_out, in1=and_2_out, out=open
  and and_2 (and_2_out, xor_1_out, in_1);
  xor xor_2 (out_4, in_1, xor_1_out);
endmodule
