// Logisim project my_counter.circ as structural Verilog: 1 circuit, main circuit main
module main (
  input  in_1,
  output [7:0] out_2
);

  wire clock_1_out;
  wire [7:0] adder_1_out;

  Register register_1 (.D(adder_1_out), .clk(clock_1_out), .Q(out_2), .clr(in_1));  // open: en
  Clock clock_1 (.out(clock_1_out));
  Adder adder_1 (.a(out_2), .b(8'h1), .out(adder_1_out));  // open: cin, cout
endmodule
