// Logisim project smallcircuit.circ as structural Verilog: 1 circuit, main circuit main
module main (
  input  in1,
  input  in2,
  input  in3,
  input  in_4
);

  wire and_1_out, and_2_out, and_3_out, notin1, notin2, notin3;

  not not_1 (notin1, in1);
  not not_2 (notin2, in2);
  not not_3 (notin3, in3);
  and and_1 (and_1_out, in1, in2, in3);
  and and_2 (and_2_out, in1, notin2, notin3);
  and and_3 (and_3_out, notin1, notin2, notin3);
  // OR_Gate or_1 has open pins: in0=and_1_out, in1=and_2_out, in2=and_3_out, out=open
endmodule
